# Fritzing sketch Pico_MCP3008 (saved by Fritzing 0.9.6b)
breadboards: 1

parts:
  ADC1 = MCP3008 [package=dil16]
  Mod1 = Raspberry Pi Pico

nets:
  N1: ADC1.DGND, ADC1.AGND, Mod1.pin_3, Mod1.pin_8, Mod1.pin_13, Mod1.pin_18, Mod1.pin_23, Mod1.pin_28, Mod1.pin_33, Mod1.pin_38, Mod1.pin_42
  N2: ADC1.CS/SHDN, Mod1.pin_7
  N3: ADC1.Din, Mod1.pin_5
  N4: ADC1.Dout, Mod1.pin_6
  N5: ADC1.CLK, Mod1.pin_4
  N6: ADC1.VREF, ADC1.VDD, Mod1.pin_36

custom parts:
  Raspberry Pi Pico: Raspberry Pi Pico. Based around the RP2040 microcontroller the Pico is a low cost microcontroller device bringing Raspberry Pi quality, cost, and easy of use to the microcontroller space. Jan 2021, Split part in to two versions: tht (this one) and SMD. This one will drill holes for a .1 in header in pcb to allow plugging in the module as well as providing pads to solder the module to the top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
